// Logisim project Logical Diagram.circ as structural Verilog: 1 circuit, main circuit main
module main (
);

  wire A1_out, A4_out, A5_out, B1_out, B2_out, B3_out, B4_out, C1_out, C2_out, C3_out, C4_out, O1_out,
       O2_out, P1_out, P2_out, Q1_out, Q2_out, Q3_out, undriven, undriven_2, undriven_3, undriven_4,
       undriven_5, undriven_6, undriven_7, undriven_8;

  and A1 (A1_out, undriven_6, undriven_7);
  and A2 (A1_out, undriven_5, undriven_4, undriven_7);
  and A3 (A1_out, undriven_5, undriven, undriven_7, undriven_2);
  and A4 (A4_out, undriven_5, undriven_2, undriven_7, undriven_3);
  and B1 (B1_out, undriven_4, undriven_5);
  and B2 (B2_out, undriven, undriven_5, undriven_2);
  and B3 (B3_out, undriven_5, undriven_2, undriven_3);
  and C1 (C1_out, undriven_2, undriven);
  and C2 (C2_out, undriven_2, undriven_3);
  or O1 (O1_out, A1_out, A1_out, A1_out, A1_out);
  or P1 (P1_out, undriven_6, B1_out, B2_out);
  or Q1 (Q1_out, undriven_4, C1_out);
  and A5 (A5_out, A4_out, undriven_8);
  and B4 (B4_out, undriven_8, B3_out);
  and C3 (C3_out, undriven_8, C2_out);
  and C4 (C4_out, undriven_8, undriven_3);
  or O2 (O2_out, O1_out, A5_out);
  or P2 (P2_out, P1_out, B4_out);
  or Q2 (Q2_out, Q1_out, C3_out);
  or Q3 (Q3_out, C4_out, undriven);

  // Notes on the sheet:
  //   g_3
  //   a_3
  //   g_2
  //   a_2
  //   g_1
  //   a_1
  //   a_0
  //   g_0
  //   A
  //   c_0
  //   G
  //   c_4
  //   c_3
  //   c_2
  //   c_1
endmodule
